# Fritzing sketch protothreads_arduino (saved by Fritzing 0.9.3b)
circuit board: 7.0417cm x 5.50703cm
breadboards: 1

parts:
  Componente1 = Arduino Uno (Rev3)
  S1 = Momentary Switch [package=ksa_sealed_tac_switch]
  LED1 = smd LED [color="Red (633nm)" package="1206 [SMD]"]
  S2 = Momentary Switch [package=ksa_sealed_tac_switch]
  LED2 = smd LED [color="Red (633nm)" package="1206 [SMD]"]
  R1 = Resistor [tolerance=±5% resistance=330 package=THT]
  LED3 = smd LED [color="Red (633nm)" package="1206 [SMD]"]
  R2 = Resistor [tolerance=±5% resistance=330 package=THT]
  R3 = Resistor [tolerance=±5% resistance=330 package=THT]

nets:
  N1: Componente1.D8, R1.Pin_0
  N2: Componente1.D9_PWM, S2.2
  N3: Componente1.D10_PWM/SS, S1.2
  N4: Componente1.D6_PWM, R3.Pin_0
  N5: Componente1.D7, R2.Pin_0
  5V: Componente1.5V
  GND: Componente1.GND, S1.4, LED1.cathode, S2.4, LED2.cathode, LED3.cathode
  N6: LED1.anode, R3.Pin_1
  N7: LED2.anode, R2.Pin_1
  N8: R1.Pin_1, LED3.anode
